# Fritzing sketch BUFFER (saved by Fritzing 1.0.1rc)
breadboards: 1

parts:
  S1 = Pushbutton [package="[THT]"]
  LED1 = LED - 5mm [color="Red (633nm)" current=0.030 package="5 mm [THT]"]
  R3 = Resistor [tolerance=±5% power=0.25 resistance=220 package=THT]
  Power_plug1 = Power plug
  Q3 = NPN-Transistor [package="TO92 [THT]"]
  R4 = Resistor [tolerance=±5% power=0.25 resistance=1k package=THT]
  R5 = Resistor [tolerance=±5% power=0.25 resistance=330 package=THT]

nets:
  N1: S1.Pin_1, S1.Pin_2, Power_plug1.VCC, Q3.C
  N2: S1.Pin_3, S1.Pin_4, R4.Pin_1
  N3: LED1.cathode, Power_plug1.GND, R5.Pin_1
  N4: LED1.anode, R3.Pin_0
  N5: R3.Pin_1, Q3.E, R5.Pin_0
  N6: Q3.B, R4.Pin_0

notes:
  Compuerta BUFFER
