# Fritzing sketch NAND (saved by Fritzing 1.0.1rc)
breadboards: 1

parts:
  S1 = Pushbutton [package="[THT]"]
  S2 = Pushbutton [package="[THT]"]
  LED1 = LED - 5mm [color="Red (633nm)" current=0.030 package="5 mm [THT]"]
  R1 = Resistor [tolerance=±5% power=0.25 resistance=2.2k package=THT]
  R3 = Resistor [tolerance=±5% power=0.25 resistance=330 package=THT]
  Power_plug1 = Power plug
  Q3 = NPN-Transistor [package="TO92 [THT]"]
  Q4 = NPN-Transistor [package="TO92 [THT]"]
  R4 = Resistor [tolerance=±5% power=0.25 resistance=1k package=THT]
  R5 = Resistor [tolerance=±5% power=0.25 resistance=1k package=THT]
  R6 = Resistor [tolerance=±5% power=0.25 resistance=330 package=THT]
  Q5 = NPN-Transistor [package="TO92 [THT]"]
  R7 = Resistor [tolerance=±5% power=0.25 resistance=2.2k package=THT]

nets:
  N1: S1.Pin_1, S1.Pin_2, S2.Pin_1, S2.Pin_2, Power_plug1.VCC
  N2: S1.Pin_3, S1.Pin_4, R7.Pin_1
  N3: S2.Pin_3, S2.Pin_4, R1.Pin_1
  N4: LED1.cathode, Power_plug1.GND, Q3.E, R6.Pin_1
  N5: LED1.anode, R3.Pin_0
  N6: R1.Pin_0, Q5.B
  N7: R3.Pin_1, Q3.C, R5.Pin_0
  N8: Q3.B, R4.Pin_0
  N9: Q4.E, R4.Pin_1, R6.Pin_0
  N10: Q4.B, R7.Pin_0
  N11: Q4.C, Q5.E
  N12: R5.Pin_1, Q5.C

notes:
  Compuerta NAND
