# Fritzing sketch NOR (saved by Fritzing 1.0.1rc)
breadboards: 1

parts:
  Q1 = NPN-Transistor [package="TO92 [THT]"]
  S1 = Pushbutton [package="[THT]"]
  Q2 = NPN-Transistor [package="TO92 [THT]"]
  S2 = Pushbutton [package="[THT]"]
  LED1 = LED - 5mm [color="Red (633nm)" current=0.030 package="5 mm [THT]"]
  R1 = Resistor [tolerance=±5% power=0.25 resistance=2.2k package=THT]
  R2 = Resistor [tolerance=±5% power=0.25 resistance=2.2k package=THT]
  R3 = Resistor [tolerance=±5% power=0.25 resistance=220 package=THT]
  Power_plug1 = Power plug
  Q3 = NPN-Transistor [package="TO92 [THT]"]
  R4 = Resistor [tolerance=±5% power=0.25 resistance=1k package=THT]
  R5 = Resistor [tolerance=±5% power=0.25 resistance=1k package=THT]
  R6 = Resistor [tolerance=±5% power=0.25 resistance=1k package=THT]

nets:
  N1: Q1.E, Q2.E, R4.Pin_0, R5.Pin_1
  N2: Q1.B, R1.Pin_0
  N3: Q1.C, S1.Pin_1, S1.Pin_2, Q2.C, S2.Pin_1, S2.Pin_2, Power_plug1.VCC, R6.Pin_1
  N4: S1.Pin_3, S1.Pin_4, R1.Pin_1
  N5: Q2.B, R2.Pin_0
  N6: S2.Pin_3, S2.Pin_4, R2.Pin_1
  N7: LED1.cathode, Power_plug1.GND, Q3.E, R4.Pin_1
  N8: LED1.anode, R3.Pin_0
  N9: R3.Pin_1, Q3.C, R6.Pin_0
  N10: Q3.B, R5.Pin_0

notes:
  Compuerta NOR
