# Fritzing sketch XNOR (saved by Fritzing 1.0.1rc)
breadboards: 1

parts:
  Q1 = NPN-Transistor [package="TO92 [THT]"]
  S1 = Pushbutton [package="[THT]"]
  Q2 = NPN-Transistor [package="TO92 [THT]"]
  S2 = Pushbutton [package="[THT]"]
  LED1 = LED - 5mm [color="Red (633nm)" current=0.030 package="5 mm [THT]"]
  R1 = Resistor [tolerance=±5% power=0.25 resistance=2.2k package=THT]
  R2 = Resistor [tolerance=±5% power=0.25 resistance=2.2k package=THT]
  R3 = Resistor [tolerance=±5% power=0.25 resistance=330 package=THT]
  Power_plug1 = Power plug
  Q3 = NPN-Transistor [package="TO92 [THT]"]
  Q4 = NPN-Transistor [package="TO92 [THT]"]
  Q5 = NPN-Transistor [package="TO92 [THT]"]
  R4 = Resistor [tolerance=±5% power=0.25 resistance=2.2k package=THT]
  Q6 = NPN-Transistor [package="TO92 [THT]"]
  R5 = Resistor [tolerance=±5% power=0.25 resistance=1k package=THT]
  R6 = Resistor [tolerance=±5% power=0.25 resistance=1k package=THT]
  R7 = Resistor [tolerance=±5% power=0.25 resistance=330 package=THT]
  R8 = Resistor [tolerance=±5% power=0.25 resistance=2.2k package=THT]
  Q7 = NPN-Transistor [package="TO92 [THT]"]
  R9 = Resistor [tolerance=±5% power=0.25 resistance=2.2k package=THT]
  Q8 = NPN-Transistor [package="TO92 [THT]"]
  R10 = Resistor [tolerance=±5% power=0.25 resistance=1k package=THT]
  R11 = Resistor [tolerance=±5% power=0.25 resistance=1k package=THT]
  R12 = Resistor [tolerance=±5% power=0.25 resistance=2.2k package=THT]
  R13 = Resistor [tolerance=±5% power=0.25 resistance=330 package=THT]
  R14 = Resistor [tolerance=±5% power=0.25 resistance=1k package=THT]
  Q9 = NPN-Transistor [package="TO92 [THT]"]
  R15 = Resistor [tolerance=±5% power=0.25 resistance=1k package=THT]
  R16 = Resistor [tolerance=±5% power=0.25 resistance=1k package=THT]

nets:
  N1: Q1.E, Q1.C, S1.Pin_1, S1.Pin_2, Q2.C, S2.Pin_1, S2.Pin_2, Power_plug1.VCC, Q3.C, R6.Pin_1, Q7.C, R11.Pin_1, R16.Pin_1
  N2: Q1.B, R9.Pin_1
  N3: S1.Pin_3, S1.Pin_4, R2.Pin_1, R5.Pin_1
  N4: Q2.E, Q5.C
  N5: Q2.B, R2.Pin_0
  N6: S2.Pin_3, S2.Pin_4, R1.Pin_1, R10.Pin_1
  N7: LED1.cathode, R3.Pin_1, Power_plug1.GND, Q6.E, R7.Pin_1, Q8.E, R12.Pin_1, R13.Pin_1, Q9.E
  N8: LED1.anode, R14.Pin_1
  N9: R1.Pin_0, Q4.B
  N10: R3.Pin_0, Q4.E, R9.Pin_0
  N11: Q3.E, Q4.C
  N12: Q3.B, R4.Pin_1
  N13: Q5.E, R7.Pin_0
  N14: Q5.B, R8.Pin_0
  N15: R4.Pin_0, Q6.B, R5.Pin_0
  N16: Q6.C, R6.Pin_0
  N17: Q7.E, R13.Pin_0, R15.Pin_0
  N18: Q7.B, R12.Pin_0
  N19: Q8.B, R10.Pin_0
  N20: Q8.C, R11.Pin_0
  N21: R14.Pin_0, Q9.C, R16.Pin_0
  N22: Q9.B, R15.Pin_1

notes:
  Compuerta XNOR
  NOT
  AND
  A
  B
  OR
  Z=not [(not A and B) or (A and not B)]
