# Fritzing sketch XORv2 (saved by Fritzing 1.0.1rc)
breadboards: 1

parts:
  Q1 = NPN-Transistor [package="TO92 [THT]"]
  S1 = Pushbutton [package="[THT]"]
  Q2 = NPN-Transistor [package="TO92 [THT]"]
  S2 = Pushbutton [package="[THT]"]
  LED1 = LED - 5mm [color="Red (633nm)" current=0.030 package="5 mm [THT]"]
  R1 = Resistor [tolerance=±5% power=0.25 resistance=2.2k package=THT]
  R2 = Resistor [tolerance=±5% power=0.25 resistance=2.2k package=THT]
  R3 = Resistor [tolerance=±5% power=0.25 resistance=330 package=THT]
  Power_plug1 = Power plug
  Q3 = NPN-Transistor [package="TO92 [THT]"]
  Q4 = NPN-Transistor [package="TO92 [THT]"]
  Q5 = NPN-Transistor [package="TO92 [THT]"]
  R4 = Resistor [tolerance=±5% power=0.25 resistance=2.2k package=THT]

nets:
  N1: Q1.E, Q2.E, Q5.C
  N2: Q1.B, S1.Pin_3, S1.Pin_4, Q3.B
  N3: Q1.C, Q2.C, LED1.cathode
  N4: S1.Pin_1, S1.Pin_2, R4.Pin_1
  N5: Q2.B, S2.Pin_3, S2.Pin_4, Q4.B
  N6: S2.Pin_1, S2.Pin_2, R1.Pin_1
  N7: LED1.anode, R3.Pin_0
  N8: R1.Pin_0, R2.Pin_0, R3.Pin_1, Power_plug1.VCC, R4.Pin_0
  N9: R2.Pin_1, Q4.C, Q5.B
  N10: Power_plug1.GND, Q3.E, Q5.E
  N11: Q3.C, Q4.E

notes:
  Compuerta XOR
